# Fritzing sketch door-key-dispenser (saved by Fritzing 0.9.9b)

parts:
  U1 = NodeMCU V3.0
  IR1 = TSOP312.., 314.. [package=THT]
  S1 = H-Bridge with L298N
  VCC1 = Battery  # not connected
  M1 = RioRand LM2596
  M2 = DC Motor

nets:
  N1: U1.D1, IR1.Data
  GND: U1.GND, IR1.GND, S1.GND, M1.Pin_4
  N2: U1.3V3, IR1.Vs
  VIN: U1.Vin, S1.5V, M1.Pin_3
  N3: S1.M2-01, M2.pin_2
  N4: S1.M2-02, M2.pin_1

custom parts:
  NodeMCU V3.0: NodeMcu V3 Lua WIFI Development Board
  H-Bridge with L298N: h-bridge
  Battery: Your standard 2x 18650 battery pack (7,4 Volts)
